# Fritzing sketch mini_proximity_sensor (saved by Fritzing 0.9.3b)
breadboards: 1

parts:
  Composant1 = Arduino Mega 2560 (Rev3)
  HC-SR04_Sensor_1 = HC-SR04 Ultrasonic Distance Sensor
  LED1 = smd LED [color="Red (633nm)" package="0603 [SMD]"]
  LED2 = smd LED [color="Green (555nm)" package="0603 [SMD]"]
  LED3 = smd LED [color="Yellow (595nm)" package="0603 [SMD]"]

nets:
  5V: Composant1.5V, HC-SR04_Sensor_1.VCC
  GND: Composant1.GND, HC-SR04_Sensor_1.GND, LED1.cathode, LED2.anode, LED3.cathode
  N1: Composant1.D5_PWM, LED1.anode
  N2: Composant1.D6_PWM, LED3.anode
  N3: Composant1.D7_PWM, LED2.cathode
  N4: Composant1.D52, HC-SR04_Sensor_1.TRIG
  N5: Composant1.D53, HC-SR04_Sensor_1.ECHO
